// Logisim project cpu.circ as structural Verilog: 3 circuits, main circuit main
module base_5_encoder (
  input  _0,
  input  _1,
  input  _2,
  input  _3,
  input  _4,
  input  _5,
  input  _6,
  input  _7,
  input  _8,
  input  _9,
  input  _10,
  input  _11,
  input  _12,
  input  _13,
  input  _14,
  input  _15,
  output Fives_digit,
  output b,
  output c,
  output d,
  output e,
  output f,
  output g,
  output a,
  output b_2,
  output c_2,
  output d_2,
  output e_2,
  output f_2,
  output g_2
);

  wire or_1_out, or_2_out, or_3_out, or_4_out, or_5_out, or_6_out, or_7_out, or_8_out, or_9_out, or_10_out,
       or_11_out, or_12_out, or_13_out, or_14_out, or_15_out, or_16_out, or_17_out, or_18_out, or_19_out,
       or_20_out, or_21_out, or_22_out, or_24_out, or_26_out, or_28_out, or_29_out, or_31_out, or_35_out;

  or or_1 (or_1_out, _0, _10);
  or or_2 (or_2_out, _1, _11);
  or or_3 (or_3_out, _2, _12);
  or or_4 (or_4_out, _3, _13);
  or or_5 (or_5_out, _4, _14);
  or or_6 (or_6_out, or_1_out, _15);
  or or_7 (or_7_out, or_6_out, _5);
  or or_8 (or_8_out, or_2_out, _6);
  or or_9 (or_9_out, or_3_out, _7);
  or or_10 (or_10_out, or_4_out, _8);
  or or_11 (or_11_out, or_5_out, _9);
  or or_12 (or_12_out, _3, _4);
  or or_13 (or_13_out, _8, _9);
  or or_14 (or_14_out, _13, _14);
  or or_15 (or_15_out, or_4_out, or_5_out);
  or or_16 (or_16_out, _2, or_12_out);
  or or_17 (or_17_out, _7, or_13_out);
  or or_18 (or_18_out, _12, or_14_out);
  or or_19 (or_19_out, or_3_out, or_15_out);
  or or_20 (or_20_out, _1, or_16_out);
  or or_21 (or_21_out, _6, or_17_out);
  or or_22 (or_22_out, _11, or_18_out);
  or or_23 (e, or_1_out, or_24_out);
  or or_24 (or_24_out, or_2_out, or_19_out);
  or or_25 (e_2, or_9_out, or_7_out);
  or or_26 (or_26_out, or_10_out, or_11_out);
  or or_27 (f, _0, or_20_out);
  or or_28 (or_28_out, _5, or_21_out);
  or or_29 (or_29_out, _10, or_22_out);
  or or_30 (a, or_10_out, e_2);
  or or_31 (or_31_out, or_26_out, or_7_out);
  or or_32 (f_2, or_11_out, or_7_out);
  or or_33 (g_2, or_26_out, or_9_out);
  or or_34 (d, _15, e);
  or or_35 (or_35_out, f, or_28_out);
  or or_36 (g, _15, or_29_out);
  or or_37 (c_2, or_8_out, or_31_out);
  or or_38 (c, _15, or_35_out);
  or or_39 (b, c_2, e_2);

  assign b_2 = b;
  assign d_2 = a;
  assign Fives_digit = d;

  // Notes on the sheet:
  //   Ones digit
  //   a
endmodule

module main (
);

  wire base_5_encoder_1_a, base_5_encoder_1_b, base_5_encoder_1_b_2, base_5_encoder_1_c,
       base_5_encoder_1_c_2, base_5_encoder_1_d, base_5_encoder_1_d_2, base_5_encoder_1_e,
       base_5_encoder_1_e_2, base_5_encoder_1_f, base_5_encoder_1_f_2, base_5_encoder_1_fives_digit,
       base_5_encoder_1_g, base_5_encoder_1_g_2, base_5_encoder_2_a, base_5_encoder_2_b,
       base_5_encoder_2_b_2, base_5_encoder_2_c, base_5_encoder_2_c_2, base_5_encoder_2_d,
       base_5_encoder_2_d_2, base_5_encoder_2_e, base_5_encoder_2_e_2, base_5_encoder_2_f,
       base_5_encoder_2_f_2, base_5_encoder_2_fives_digit, base_5_encoder_2_g, base_5_encoder_2_g_2,
       dipswitch_1_sw1, dipswitch_1_sw2, dipswitch_1_sw3, dipswitch_1_sw4, dipswitch_1_sw5, dipswitch_1_sw6,
       dipswitch_1_sw7, dipswitch_1_sw8, dipswitch_1_sw9, dipswitch_1_sw10, dipswitch_1_sw11,
       dipswitch_1_sw12, dipswitch_1_sw13, dipswitch_1_sw14, dipswitch_1_sw15, dipswitch_1_sw16,
       dipswitch_2_sw1, dipswitch_2_sw2, dipswitch_2_sw3, dipswitch_2_sw4, dipswitch_2_sw5, dipswitch_2_sw6,
       dipswitch_2_sw7, dipswitch_2_sw8, dipswitch_2_sw9, dipswitch_2_sw10, dipswitch_2_sw11,
       dipswitch_2_sw12, dipswitch_2_sw13, dipswitch_2_sw14, dipswitch_2_sw15, dipswitch_2_sw16;

  _7_Segment_Display u_7_segment_display_1 (
    .g(base_5_encoder_1_g), .f(base_5_encoder_1_f), .a(base_5_encoder_1_fives_digit), .b(base_5_encoder_1_b),
    .e(base_5_encoder_1_e), .d(base_5_encoder_1_d), .c(base_5_encoder_1_c));  // open: dp
  base_5_encoder base_5_encoder_1 (
    .f_2(base_5_encoder_1_f_2), .g_2(base_5_encoder_1_g_2), .a(base_5_encoder_1_a),
    .b_2(base_5_encoder_1_b_2), .c_2(base_5_encoder_1_c_2), .d_2(base_5_encoder_1_d_2),
    .e_2(base_5_encoder_1_e_2), .Fives_digit(base_5_encoder_1_fives_digit), .b(base_5_encoder_1_b),
    .c(base_5_encoder_1_c), .d(base_5_encoder_1_d), .e(base_5_encoder_1_e), .f(base_5_encoder_1_f),
    .g(base_5_encoder_1_g), ._9(dipswitch_1_sw10), ._10(dipswitch_1_sw11), ._11(dipswitch_1_sw12),
    ._12(dipswitch_1_sw13), ._13(dipswitch_1_sw14), ._14(dipswitch_1_sw15), ._15(dipswitch_1_sw16),
    ._0(dipswitch_1_sw1), ._1(dipswitch_1_sw2), ._2(dipswitch_1_sw3), ._3(dipswitch_1_sw4),
    ._4(dipswitch_1_sw5), ._5(dipswitch_1_sw6), ._6(dipswitch_1_sw7), ._7(dipswitch_1_sw8),
    ._8(dipswitch_1_sw9));
  DipSwitch #(.number(16)) dipswitch_1 (
    .sw1(dipswitch_1_sw1), .sw2(dipswitch_1_sw2), .sw3(dipswitch_1_sw3), .sw4(dipswitch_1_sw4),
    .sw5(dipswitch_1_sw5), .sw6(dipswitch_1_sw6), .sw7(dipswitch_1_sw7), .sw8(dipswitch_1_sw8),
    .sw9(dipswitch_1_sw9), .sw10(dipswitch_1_sw10), .sw11(dipswitch_1_sw11), .sw12(dipswitch_1_sw12),
    .sw13(dipswitch_1_sw13), .sw14(dipswitch_1_sw14), .sw15(dipswitch_1_sw15), .sw16(dipswitch_1_sw16));
  _7_Segment_Display u_7_segment_display_2 (
    .g(base_5_encoder_1_g_2), .f(base_5_encoder_1_f_2), .a(base_5_encoder_1_a), .b(base_5_encoder_1_b_2),
    .e(base_5_encoder_1_e_2), .d(base_5_encoder_1_d_2), .c(base_5_encoder_1_c_2));  // open: dp
  base_2_encoder base_2_encoder_1 (
    ._0(dipswitch_1_sw1), ._1(dipswitch_1_sw2), ._2(dipswitch_1_sw3), ._3(dipswitch_1_sw4),
    ._4(dipswitch_1_sw5), ._5(dipswitch_1_sw6), ._6(dipswitch_1_sw7), ._7(dipswitch_1_sw8),
    ._8(dipswitch_1_sw9), ._9(dipswitch_1_sw10), ._10(dipswitch_1_sw11), ._11(dipswitch_1_sw12),
    ._12(dipswitch_1_sw13), ._13(dipswitch_1_sw14), ._14(dipswitch_1_sw15), ._15(dipswitch_1_sw16));  // open: A0, A1, A2, A3
  _7_Segment_Display u_7_segment_display_3 (
    .g(base_5_encoder_2_g), .f(base_5_encoder_2_f), .a(base_5_encoder_2_fives_digit), .b(base_5_encoder_2_b),
    .e(base_5_encoder_2_e), .d(base_5_encoder_2_d), .c(base_5_encoder_2_c));  // open: dp
  base_5_encoder base_5_encoder_2 (
    .f_2(base_5_encoder_2_f_2), .g_2(base_5_encoder_2_g_2), .a(base_5_encoder_2_a),
    .b_2(base_5_encoder_2_b_2), .c_2(base_5_encoder_2_c_2), .d_2(base_5_encoder_2_d_2),
    .e_2(base_5_encoder_2_e_2), .Fives_digit(base_5_encoder_2_fives_digit), .b(base_5_encoder_2_b),
    .c(base_5_encoder_2_c), .d(base_5_encoder_2_d), .e(base_5_encoder_2_e), .f(base_5_encoder_2_f),
    .g(base_5_encoder_2_g), ._9(dipswitch_2_sw10), ._10(dipswitch_2_sw11), ._11(dipswitch_2_sw12),
    ._12(dipswitch_2_sw13), ._13(dipswitch_2_sw14), ._14(dipswitch_2_sw15), ._15(dipswitch_2_sw16),
    ._0(dipswitch_2_sw1), ._1(dipswitch_2_sw2), ._2(dipswitch_2_sw3), ._3(dipswitch_2_sw4),
    ._4(dipswitch_2_sw5), ._5(dipswitch_2_sw6), ._6(dipswitch_2_sw7), ._7(dipswitch_2_sw8),
    ._8(dipswitch_2_sw9));
  DipSwitch #(.number(16)) dipswitch_2 (
    .sw1(dipswitch_2_sw1), .sw2(dipswitch_2_sw2), .sw3(dipswitch_2_sw3), .sw4(dipswitch_2_sw4),
    .sw5(dipswitch_2_sw5), .sw6(dipswitch_2_sw6), .sw7(dipswitch_2_sw7), .sw8(dipswitch_2_sw8),
    .sw9(dipswitch_2_sw9), .sw10(dipswitch_2_sw10), .sw11(dipswitch_2_sw11), .sw12(dipswitch_2_sw12),
    .sw13(dipswitch_2_sw13), .sw14(dipswitch_2_sw14), .sw15(dipswitch_2_sw15), .sw16(dipswitch_2_sw16));
  _7_Segment_Display u_7_segment_display_4 (
    .g(base_5_encoder_2_g_2), .f(base_5_encoder_2_f_2), .a(base_5_encoder_2_a), .b(base_5_encoder_2_b_2),
    .e(base_5_encoder_2_e_2), .d(base_5_encoder_2_d_2), .c(base_5_encoder_2_c_2));  // open: dp
  base_2_encoder base_2_encoder_2 (
    ._0(dipswitch_2_sw1), ._1(dipswitch_2_sw2), ._2(dipswitch_2_sw3), ._3(dipswitch_2_sw4),
    ._4(dipswitch_2_sw5), ._5(dipswitch_2_sw6), ._6(dipswitch_2_sw7), ._7(dipswitch_2_sw8),
    ._8(dipswitch_2_sw9), ._9(dipswitch_2_sw10), ._10(dipswitch_2_sw11), ._11(dipswitch_2_sw12),
    ._12(dipswitch_2_sw13), ._13(dipswitch_2_sw14), ._14(dipswitch_2_sw15), ._15(dipswitch_2_sw16));  // open: A0, A1, A2, A3

  // Notes on the sheet:
  //   Input 1
  //   Input 2
endmodule

module base_2_encoder (
  input  _0,
  input  _1,
  input  _2,
  input  _3,
  input  _4,
  input  _5,
  input  _6,
  input  _7,
  input  _8,
  input  _9,
  input  _10,
  input  _11,
  input  _12,
  input  _13,
  input  _14,
  input  _15,
  output A0,
  output A1,
  output A2,
  output A3
);

  wire or_1_out, or_2_out, or_3_out, or_4_out, or_5_out, or_6_out, or_7_out, or_8_out, or_9_out, or_10_out,
       or_11_out, or_12_out, or_13_out, or_14_out, or_15_out, or_16_out, or_17_out, or_18_out;

  or or_1 (or_1_out, _13, _15);
  or or_2 (or_2_out, _2, _3);
  or or_3 (or_3_out, _4, _5);
  or or_4 (or_4_out, _6, _7);
  or or_5 (or_5_out, _8, _9);
  or or_6 (or_6_out, _10, _11);
  or or_7 (or_7_out, _12, _13);
  or or_8 (or_8_out, _14, _15);
  or or_9 (or_9_out, _11, or_1_out);
  or or_10 (or_10_out, _9, or_9_out);
  or or_11 (or_11_out, or_2_out, or_4_out);
  or or_12 (or_12_out, or_3_out, or_4_out);
  or or_13 (or_13_out, _5, or_14_out);
  or or_14 (or_14_out, _7, or_10_out);
  or or_15 (or_15_out, or_6_out, or_8_out);
  or or_16 (or_16_out, or_5_out, or_6_out);
  or or_17 (or_17_out, or_7_out, or_8_out);
  or or_18 (or_18_out, _3, or_13_out);
  or or_19 (A0, _1, or_18_out);
  or or_20 (A1, or_11_out, or_15_out);
  or or_21 (A2, or_12_out, or_17_out);
  or or_22 (A3, or_16_out, or_17_out);
endmodule
